# Fritzing sketch door secu (saved by Fritzing 0.9.3b)
breadboards: 1

parts:
  Part1 = Arduino Uno (Rev3)
  hc-sr1 = hc-sr04
  SG1 = Buzzer 12mm [package=buzzer-ccv]
  Matrix_keypad2 = KEYPAD 4x4

nets:
  N1: Part1.A0, Matrix_keypad2.col1
  N2: Part1.A1, Matrix_keypad2.col2
  N3: Part1.A2, Matrix_keypad2.col3
  N4: Part1.A3, Matrix_keypad2.col4
  N5: Part1.D11_PWM/MOSI, SG1.1
  N6: Part1.D12/MISO, hc-sr1.Echo
  N7: Part1.D13/SCK, hc-sr1.Trig
  N8: Part1.D0/RX, Matrix_keypad2.row3
  N9: Part1.D1/TX, Matrix_keypad2.row2
  N10: Part1.D2, Matrix_keypad2.row1
  5V: Part1.5V, hc-sr1.VCC
  GND: Part1.GND, hc-sr1.GND, SG1.2

custom parts:
  KEYPAD 4x4: Matrix keypad 16 buttons, 4 rows x 4 columns

// code stored in the sketch: Ultrasonic Sensor code.ino
/*
please give credit to the man who made the code,Roibal @ https://github.com/Roibal/arduino_sbs/blob/65147f784619eb0ba8a6db107d4d958404c95463/Ultrasonic%20Distance%20Sensor/Distance/DistanceTempUltrasonic.ino
HC-SR04 Ping distance sensor]
Temperature Sensor TMP36
VCC to arduino 5v GND to arduino GND
Echo to Arduino pin 12 Trig to Arduino pin 13
Red POS to Arduino pin 11
Green POS to Arduino pin 10
Analog 0 to TMP36
Original code improvements to the Ping sketch sourced from Trollmaker.com
Some code and wiring inspired by http://en.wikiversity.org/wiki/User:Dstaub/robotcar
Additional code added to adjust speed of sound based on temperature modified from SparkFun code
*/

// We'll use analog input 0 to measure the temperature sensor's
// signal pin.

const int temperaturePin = 0; 


#define trigPin 13
#define echoPin 12

void setup() {
  Serial.begin (9600);
  pinMode(trigPin, OUTPUT);
  pinMode(echoPin, INPUT);
}

void loop() {
  long duration, distance;
  float voltage, degreesC, degreesF, speedOfSound;

  // First we'll measure the voltage at the analog pin. Normally
  // we'd use analogRead(), which returns a number from 0 to 1023.
  // Here we've written a function (further down) called
  // getVoltage() that returns the true voltage (0 to 5 Volts)
  // present on an analog input pin.

  voltage = getVoltage(temperaturePin);
  
  // Now we'll convert the voltage to degrees Celsius.
  // This formula comes from the temperature sensor datasheet:

  degreesC = (voltage - 0.5) * 100.0;
  
  // While we're at it, let's convert degrees Celsius to Fahrenheit.
  // This is the classic C to F conversion formula:
  
  degreesF = degreesC * (9.0/5.0) + 32.0;
    
  digitalWrite(trigPin, LOW);  // Added this line
  delayMicroseconds(2); // Added this line
  digitalWrite(trigPin, HIGH);
//  delayMicroseconds(1000); - Removed this line
  delayMicroseconds(10); // Added this line
  digitalWrite(trigPin, LOW);
  duration = pulseIn(echoPin, HIGH);
  speedOfSound = (degreesC * 0.6 + 331.5)/10000;
  distance = (duration/2) * speedOfSound; //includes Speed of Sound conversion factor into centimeters and micro seconds

  if (distance >= 200 || distance <= 0){
    Serial.print("  deg C: ");
    Serial.print(degreesC);
    Serial.print("   ");
    Serial.print(speedOfSound);
    Serial.println("Out of range");
    
  }
  else {
    Serial.print("  deg C: ");
    Serial.print(degreesC);
    Serial.print("   ");
    Serial.print(distance);
    Serial.println(" cm");
  }
  delay(500);
}


float getVoltage(int pin)
{

  return (analogRead(pin) * 0.004882814);
}
